// Logisim project des.circ as structural Verilog: 23 circuits, main circuit main
module main (
  input  enable,
  input  [63:0] in_data,
  input  [55:0] key,
  input  mode,
  output [63:0] out_data
);

  // DEScoder descoder_1: pin names not known; wires that end beside it: enable, in_data, key, mode, out_data
endmodule

module DEScoder (
  input  mode,
  input  [55:0] key,
  input  enable,
  input  [63:0] in_data,
  output [63:0] out_data,
  output [63:0] IP_T,
  output [31:0] R0,
  output [63:0] out_8,
  output [31:0] L0,
  output [31:0] out_10,
  output [31:0] out_11
);

  wire [27:0] C1, C2, C3, C4, C5, C6, C7, C8, C9, C10, C11, C12, C13, C14, C15, C16, D1, D2, D3, D4, D5, D6,
       D7, D8, D9, D10, D11, D12, D13, D14, D15, D16, key_scheduling_1_c, key_scheduling_1_d;
  wire [31:0] circle_1_l_i, circle_1_r_i, circle_2_r_i, circle_3_l_i, circle_3_r_i, circle_4_l_i,
       circle_4_r_i, circle_5_l_i, circle_5_r_i, circle_6_l_i, circle_6_r_i, circle_7_l_i, circle_7_r_i,
       circle_8_l_i, circle_8_r_i, circle_9_l_i, circle_9_r_i, circle_10_l_i, circle_10_r_i, circle_11_l_i,
       circle_11_r_i, circle_12_l_i, circle_12_r_i, circle_13_l_i, circle_13_r_i, circle_14_l_i,
       circle_14_r_i, circle_15_l_i, circle_15_r_i, circle_16_l_i, circle_16_r_i, circle_17_l_i,
       circle_17_r_i, reversecircle_1_l_i, reversecircle_1_r_i, reversecircle_2_l_i, reversecircle_3_l_i,
       reversecircle_3_r_i, reversecircle_4_l_i, reversecircle_4_r_i, reversecircle_5_l_i,
       reversecircle_5_r_i, reversecircle_6_l_i, reversecircle_6_r_i, reversecircle_7_l_i,
       reversecircle_7_r_i, reversecircle_8_l_i, reversecircle_8_r_i, reversecircle_9_l_i,
       reversecircle_9_r_i, reversecircle_10_l_i, reversecircle_10_r_i, reversecircle_11_l_i,
       reversecircle_11_r_i, reversecircle_12_l_i, reversecircle_12_r_i, reversecircle_13_l_i,
       reversecircle_13_r_i, reversecircle_14_l_i, reversecircle_14_r_i, reversecircle_15_l_i,
       reversecircle_15_r_i, reversecircle_16_l_i, reversecircle_16_r_i;
  wire [47:0] K1, K2, K3, K4, K5, K6, K7, K8, K9, K10, K11, K12, K13, K14, K15, K16;

  key_scheduling key_scheduling_1 (.in_1(key), .C(key_scheduling_1_c), .D(key_scheduling_1_d));  // open: out_3
  joining joining_1 (.C(C1), .D(D1), .Key(K1));
  InitialPremut initialpremut_1 (.in_1(in_data), .R(out_10), .L(out_11));  // open: out_2
  shift_key1 shift_key1_1 (.in_1(key_scheduling_1_c), .out_2(C1));
  shift_key1 shift_key1_2 (.in_1(key_scheduling_1_d), .out_2(D1));
  InitialPremut initialpremut_2 (.in_1(in_data), .out_2(IP_T), .R(R0), .L(L0));
  joining joining_2 (.C(C2), .D(D2), .Key(K2));
  shift_key1 shift_key1_3 (.in_1(C1), .out_2(C2));
  shift_key1 shift_key1_4 (.in_1(D1), .out_2(D2));
  reversecircle reversecircle_1 (
    .key(K16), .Li(out_11), .Ri(out_10), .L_i(reversecircle_1_l_i), .R_i(reversecircle_1_r_i));
  joining joining_3 (.C(C3), .D(D3), .Key(K3));
  circle circle_1 (.key(K1), .Ri(R0), .Li(L0), .R_i(circle_1_r_i), .L_i(circle_1_l_i));
  circle circle_2 (.key(K16), .Ri(out_11), .Li(out_10), .R_i(circle_2_r_i));  // open: L_i
  // Probe on circle_2_r_i
  reversecircle reversecircle_2 (
    .key(K15), .Li(reversecircle_1_l_i), .Ri(reversecircle_1_r_i), .L_i(reversecircle_2_l_i),
    .R_i(reversecircle_2_l_i));
  shift_key2 shift_key2_1 (.in_1(C2), .out_2(C3));
  shift_key2 shift_key2_2 (.in_1(D2), .out_2(D3));
  circle circle_3 (.key(K2), .Ri(circle_1_r_i), .Li(circle_1_l_i), .R_i(circle_3_r_i), .L_i(circle_3_l_i));
  joining joining_4 (.C(C4), .D(D4), .Key(K4));
  reversecircle reversecircle_3 (
    .key(K14), .Li(reversecircle_2_l_i), .Ri(reversecircle_2_l_i), .L_i(reversecircle_3_l_i),
    .R_i(reversecircle_3_r_i));
  circle circle_4 (.key(K3), .Ri(circle_3_r_i), .Li(circle_3_l_i), .R_i(circle_4_r_i), .L_i(circle_4_l_i));
  shift_key2 shift_key2_3 (.in_1(C3), .out_2(C4));
  shift_key2 shift_key2_4 (.in_1(D3), .out_2(D4));
  reversecircle reversecircle_4 (
    .key(K13), .Li(reversecircle_3_l_i), .Ri(reversecircle_3_r_i), .L_i(reversecircle_4_l_i),
    .R_i(reversecircle_4_r_i));
  joining joining_5 (.C(C5), .D(D5), .Key(K5));
  circle circle_5 (.key(K4), .Ri(circle_4_r_i), .Li(circle_4_l_i), .R_i(circle_5_r_i), .L_i(circle_5_l_i));
  reversecircle reversecircle_5 (
    .key(K12), .Li(reversecircle_4_l_i), .Ri(reversecircle_4_r_i), .L_i(reversecircle_5_l_i),
    .R_i(reversecircle_5_r_i));
  shift_key2 shift_key2_5 (.in_1(C4), .out_2(C5));
  shift_key2 shift_key2_6 (.in_1(D4), .out_2(D5));
  joining joining_6 (.C(C6), .D(D6), .Key(K6));
  circle circle_6 (.key(K5), .Ri(circle_5_r_i), .Li(circle_5_l_i), .R_i(circle_6_r_i), .L_i(circle_6_l_i));
  reversecircle reversecircle_6 (
    .key(K11), .Li(reversecircle_5_l_i), .Ri(reversecircle_5_r_i), .L_i(reversecircle_6_l_i),
    .R_i(reversecircle_6_r_i));
  shift_key2 shift_key2_7 (.in_1(C5), .out_2(C6));
  shift_key2 shift_key2_8 (.in_1(D5), .out_2(D6));
  circle circle_7 (.key(K6), .Ri(circle_6_r_i), .Li(circle_6_l_i), .R_i(circle_7_r_i), .L_i(circle_7_l_i));
  reversecircle reversecircle_7 (
    .key(K10), .Li(reversecircle_6_l_i), .Ri(reversecircle_6_r_i), .L_i(reversecircle_7_l_i),
    .R_i(reversecircle_7_r_i));
  joining joining_7 (.C(C7), .D(D7), .Key(K7));
  circle circle_8 (.key(K7), .Ri(circle_7_r_i), .Li(circle_7_l_i), .R_i(circle_8_r_i), .L_i(circle_8_l_i));
  reversecircle reversecircle_8 (
    .key(K9), .Li(reversecircle_7_l_i), .Ri(reversecircle_7_r_i), .L_i(reversecircle_8_l_i),
    .R_i(reversecircle_8_r_i));
  shift_key2 shift_key2_9 (.in_1(C6), .out_2(C7));
  shift_key2 shift_key2_10 (.in_1(D6), .out_2(D7));
  joining joining_8 (.C(C8), .D(D8), .Key(K8));
  circle circle_9 (.key(K8), .Ri(circle_8_r_i), .Li(circle_8_l_i), .R_i(circle_9_r_i), .L_i(circle_9_l_i));
  reversecircle reversecircle_9 (
    .key(K8), .Li(reversecircle_8_l_i), .Ri(reversecircle_8_r_i), .L_i(reversecircle_9_l_i),
    .R_i(reversecircle_9_r_i));
  shift_key2 shift_key2_11 (.in_1(C7), .out_2(C8));
  shift_key2 shift_key2_12 (.in_1(D7), .out_2(D8));
  circle circle_10 (.key(K9), .Ri(circle_9_r_i), .Li(circle_9_l_i), .R_i(circle_10_r_i), .L_i(circle_10_l_i));
  reversecircle reversecircle_10 (
    .key(K7), .Li(reversecircle_9_l_i), .Ri(reversecircle_9_r_i), .L_i(reversecircle_10_l_i),
    .R_i(reversecircle_10_r_i));
  joining joining_9 (.C(C9), .D(D9), .Key(K9));
  circle circle_11 (.key(K10), .Ri(circle_10_r_i), .Li(circle_10_l_i), .R_i(circle_11_r_i), .L_i(circle_11_l_i));
  reversecircle reversecircle_11 (
    .key(K6), .Li(reversecircle_10_l_i), .Ri(reversecircle_10_r_i), .L_i(reversecircle_11_l_i),
    .R_i(reversecircle_11_r_i));
  shift_key1 shift_key1_5 (.in_1(C8), .out_2(C9));
  shift_key1 shift_key1_6 (.in_1(D8), .out_2(D9));
  joining joining_10 (.C(C10), .D(D10), .Key(K10));
  circle circle_12 (.key(K11), .Ri(circle_11_r_i), .Li(circle_11_l_i), .R_i(circle_12_r_i), .L_i(circle_12_l_i));
  reversecircle reversecircle_12 (
    .key(K5), .Li(reversecircle_11_l_i), .Ri(reversecircle_11_r_i), .L_i(reversecircle_12_l_i),
    .R_i(reversecircle_12_r_i));
  shift_key2 shift_key2_13 (.in_1(C9), .out_2(C10));
  shift_key2 shift_key2_14 (.in_1(D9), .out_2(D10));
  joining joining_11 (.C(C11), .D(D11), .Key(K11));
  circle circle_13 (.key(K12), .Ri(circle_12_r_i), .Li(circle_12_l_i), .R_i(circle_13_r_i), .L_i(circle_13_l_i));
  reversecircle reversecircle_13 (
    .key(K4), .Li(reversecircle_12_l_i), .Ri(reversecircle_12_r_i), .L_i(reversecircle_13_l_i),
    .R_i(reversecircle_13_r_i));
  reversecircle reversecircle_14 (
    .key(K3), .Li(reversecircle_13_l_i), .Ri(reversecircle_13_r_i), .L_i(reversecircle_14_l_i),
    .R_i(reversecircle_14_r_i));
  shift_key2 shift_key2_15 (.in_1(C10), .out_2(C11));
  shift_key2 shift_key2_16 (.in_1(D10), .out_2(D11));
  circle circle_14 (.key(K13), .Ri(circle_13_r_i), .Li(circle_13_l_i), .R_i(circle_14_r_i), .L_i(circle_14_l_i));
  joining joining_12 (.C(C12), .D(D12), .Key(K12));
  circle circle_15 (.key(K14), .Ri(circle_14_r_i), .Li(circle_14_l_i), .R_i(circle_15_r_i), .L_i(circle_15_l_i));
  reversecircle reversecircle_15 (
    .key(K2), .Li(reversecircle_14_l_i), .Ri(reversecircle_14_r_i), .L_i(reversecircle_15_l_i),
    .R_i(reversecircle_15_r_i));
  shift_key2 shift_key2_17 (.in_1(C11), .out_2(C12));
  shift_key2 shift_key2_18 (.in_1(D11), .out_2(D12));
  joining joining_13 (.C(C13), .D(D13), .Key(K13));
  circle circle_16 (.key(K15), .Ri(circle_15_r_i), .Li(circle_15_l_i), .R_i(circle_16_r_i), .L_i(circle_16_l_i));
  reversecircle reversecircle_16 (
    .key(K1), .Li(reversecircle_15_l_i), .Ri(reversecircle_15_r_i), .L_i(reversecircle_16_l_i),
    .R_i(reversecircle_16_r_i));
  shift_key2 shift_key2_19 (.in_1(C12), .out_2(C13));
  shift_key2 shift_key2_20 (.in_1(D12), .out_2(D13));
  // Probe on circle_17_r_i
  circle circle_17 (.key(K16), .Ri(circle_16_r_i), .Li(circle_16_l_i), .R_i(circle_17_r_i), .L_i(circle_17_l_i));
  FinalPermutation finalpermutation_1 (.L(reversecircle_16_l_i), .R(reversecircle_16_r_i), .IP_ans(out_8));
  joining joining_14 (.C(C14), .D(D14), .Key(K14));
  // Probe on circle_17_l_i
  shift_key2 shift_key2_21 (.in_1(C13), .out_2(C14));
  shift_key2 shift_key2_22 (.in_1(D13), .out_2(D14));
  FinalPermutation finalpermutation_2 (.L(circle_17_l_i), .R(circle_17_r_i), .IP_ans(out_data));
  joining joining_15 (.C(C15), .D(D15), .Key(K15));
  shift_key2 shift_key2_23 (.in_1(C14), .out_2(C15));
  shift_key2 shift_key2_24 (.in_1(D14), .out_2(D15));
  joining joining_16 (.C(C16), .D(D16), .Key(K16));
  shift_key1 shift_key1_7 (.in_1(C15), .out_2(C16));
  shift_key1 shift_key1_8 (.in_1(D15), .out_2(D16));

  // Notes on the sheet:
  //   Key_1
endmodule

module InitialPremut (
  input  [63:0] in_1,
  output [63:0] out_2,
  output [31:0] R,
  output [31:0] L
);

  splitting splitting_1 (
    .in_1({in_1[6], in_1[14], in_1[22], in_1[30], in_1[38], in_1[46], in_1[54], in_1[62], in_1[4], in_1[12], in_1[20], in_1[28], in_1[36], in_1[44], in_1[52], in_1[60], in_1[2], in_1[10], in_1[18], in_1[26], in_1[34], in_1[42], in_1[50], in_1[58], in_1[0], in_1[8], in_1[16], in_1[24], in_1[32], in_1[40], in_1[48], in_1[56], in_1[7], in_1[15], in_1[23], in_1[31], in_1[39], in_1[47], in_1[55], in_1[63], in_1[5], in_1[13], in_1[21], in_1[29], in_1[37], in_1[45], in_1[53], in_1[61], in_1[3], in_1[11], in_1[19], in_1[27], in_1[35], in_1[43], in_1[51], in_1[59], in_1[1], in_1[9], in_1[17], in_1[25], in_1[33], in_1[41], in_1[49], in_1[57]}),
    .R(R), .L(L));

  assign out_2 = {in_1[6], in_1[14], in_1[22], in_1[30], in_1[38], in_1[46], in_1[54], in_1[62], in_1[4], in_1[12], in_1[20], in_1[28], in_1[36], in_1[44], in_1[52], in_1[60], in_1[2], in_1[10], in_1[18], in_1[26], in_1[34], in_1[42], in_1[50], in_1[58], in_1[0], in_1[8], in_1[16], in_1[24], in_1[32], in_1[40], in_1[48], in_1[56], in_1[7], in_1[15], in_1[23], in_1[31], in_1[39], in_1[47], in_1[55], in_1[63], in_1[5], in_1[13], in_1[21], in_1[29], in_1[37], in_1[45], in_1[53], in_1[61], in_1[3], in_1[11], in_1[19], in_1[27], in_1[35], in_1[43], in_1[51], in_1[59], in_1[1], in_1[9], in_1[17], in_1[25], in_1[33], in_1[41], in_1[49], in_1[57]};

  // Other names for the same wires on the sheet: i7 = in_1[57]; i15 = in_1[49]; i23 = in_1[41]; i31 = in_1[33];
  //   i39 = in_1[25]; i47 = in_1[17]; i55 = in_1[9]; i63 = in_1[1]; i5 = in_1[59]; i13 = in_1[51]; i21 = in_1[43];
  //   i29 = in_1[35]; i37 = in_1[27]; i45 = in_1[19]; i53 = in_1[11]; i61 = in_1[3]; i3 = in_1[61]; i11 = in_1[53];
  //   i19 = in_1[45]; i27 = in_1[37]; i35 = in_1[29]; i43 = in_1[21]; i51 = in_1[13]; i59 = in_1[5]; i1 = in_1[63];
  //   i9 = in_1[55]; i17 = in_1[47]; i25 = in_1[39]; i33 = in_1[31]; i41 = in_1[23]; i49 = in_1[15]; i57 = in_1[7];
  //   i8 = in_1[56]; i16 = in_1[48]; i24 = in_1[40]; i32 = in_1[32]; i40 = in_1[24]; i48 = in_1[16]; i56 = in_1[8];
  //   i64 = in_1[0]; i6 = in_1[58]; i14 = in_1[50]; i22 = in_1[42]; i30 = in_1[34]; i38 = in_1[26]; i46 = in_1[18];
  //   i54 = in_1[10]; i62 = in_1[2]; i4 = in_1[60]; i12 = in_1[52]; i20 = in_1[44]; i28 = in_1[36]; i36 = in_1[28];
  //   i44 = in_1[20]; i52 = in_1[12]; i60 = in_1[4]; i2 = in_1[62]; i10 = in_1[54]; i18 = in_1[46]; i26 = in_1[38];
  //   i34 = in_1[30]; i42 = in_1[22]; i50 = in_1[14]; i58 = in_1[6]
endmodule

module splitting (
  input  [63:0] in_1,
  output [31:0] R,
  output [31:0] L
);


  assign L = in_1[63:32];
  assign R = in_1[31:0];

  // Other names for the same wires on the sheet: i33 = in_1[32]; i34 = in_1[33]; i35 = in_1[34]; i36 = in_1[35];
  //   i37 = in_1[36]; i38 = in_1[37]; i39 = in_1[38]; i40 = in_1[39]; i41 = in_1[40]; i42 = in_1[41]; i43 = in_1[42];
  //   i44 = in_1[43]; i45 = in_1[44]; i46 = in_1[45]; i47 = in_1[46]; i48 = in_1[47]; i49 = in_1[48]; i50 = in_1[49];
  //   i51 = in_1[50]; i52 = in_1[51]; i53 = in_1[52]; i54 = in_1[53]; i55 = in_1[54]; i56 = in_1[55]; i57 = in_1[56];
  //   i58 = in_1[57]; i59 = in_1[58]; i60 = in_1[59]; i61 = in_1[60]; i62 = in_1[61]; i63 = in_1[62]; i64 = in_1[63];
  //   i1 = in_1[0]; i2 = in_1[1]; i3 = in_1[2]; i4 = in_1[3]; i5 = in_1[4]; i6 = in_1[5]; i7 = in_1[6]; i8 = in_1[7];
  //   i9 = in_1[8]; i10 = in_1[9]; i11 = in_1[10]; i12 = in_1[11]; i13 = in_1[12]; i14 = in_1[13]; i15 = in_1[14];
  //   i16 = in_1[15]; i17 = in_1[16]; i18 = in_1[17]; i19 = in_1[18]; i20 = in_1[19]; i21 = in_1[20]; i22 = in_1[21];
  //   i23 = in_1[22]; i24 = in_1[23]; i25 = in_1[24]; i26 = in_1[25]; i27 = in_1[26]; i28 = in_1[27]; i29 = in_1[28];
  //   i30 = in_1[29]; i31 = in_1[30]; i32 = in_1[31]
endmodule

module Expansion_E (
  input  [31:0] in_1,
  output [47:0] out_2
);


  assign out_2 = {in_1[0], in_1[31:27], in_1[28:23], in_1[24:19], in_1[20:15], in_1[16:11], in_1[12:7], in_1[8:3], in_1[4:0], in_1[31]};

  // Other names for the same wires on the sheet: i31 = in_1[1]; i30 = in_1[2]; i29 = in_1[3]; i28 = in_1[4];
  //   i27 = in_1[5]; i26 = in_1[6]; i25 = in_1[7]; i24 = in_1[8]; i23 = in_1[9]; i22 = in_1[10]; i21 = in_1[11];
  //   i20 = in_1[12]; i19 = in_1[13]; i18 = in_1[14]; i17 = in_1[15]; i16 = in_1[16]; i15 = in_1[17]; i14 = in_1[18];
  //   i13 = in_1[19]; i12 = in_1[20]; i11 = in_1[21]; i10 = in_1[22]; i9 = in_1[23]; i8 = in_1[24]; i7 = in_1[25];
  //   i6 = in_1[26]; i5 = in_1[27]; i4 = in_1[28]; i3 = in_1[29]; i2 = in_1[30]; i1 = in_1[31]; i32 = in_1[0]
endmodule

module key_scheduling (
  input  [55:0] in_1,
  output [27:0] C,
  output [63:0] out_3,
  output [27:0] D
);

  wire xor_1_out, xor_2_out, xor_3_out, xor_4_out, xor_5_out, xor_6_out, xor_7_out, xor_8_out;

  ExactlyOne xor_1 (
    .out(xor_1_out), .in0(in_1[55]), .in1(in_1[54]), .in2(in_1[53]), .in3(in_1[52]), .in4(in_1[51]),
    .in5(in_1[50]), .in6(in_1[49]));
  ExactlyOne xor_2 (
    .out(xor_2_out), .in0(in_1[48]), .in1(in_1[47]), .in2(in_1[46]), .in3(in_1[45]), .in4(in_1[44]),
    .in5(in_1[43]), .in6(in_1[42]));
  ExactlyOne xor_3 (
    .out(xor_3_out), .in0(in_1[41]), .in1(in_1[40]), .in2(in_1[39]), .in3(in_1[38]), .in4(in_1[37]),
    .in5(in_1[36]), .in6(in_1[35]));
  not not_1 (out_3[56], xor_1_out);
  not not_2 (out_3[48], xor_2_out);
  not not_3 (out_3[40], xor_3_out);
  ExactlyOne xor_4 (
    .out(xor_4_out), .in0(in_1[34]), .in1(in_1[33]), .in2(in_1[32]), .in3(in_1[31]), .in4(in_1[30]),
    .in5(in_1[29]), .in6(in_1[28]));
  not not_4 (out_3[32], xor_4_out);
  ExactlyOne xor_5 (
    .out(xor_5_out), .in0(in_1[27]), .in1(in_1[26]), .in2(in_1[25]), .in3(in_1[24]), .in4(in_1[23]),
    .in5(in_1[22]), .in6(in_1[21]));
  not not_5 (out_3[24], xor_5_out);
  ExactlyOne xor_6 (
    .out(xor_6_out), .in0(in_1[20]), .in1(in_1[19]), .in2(in_1[18]), .in3(in_1[17]), .in4(in_1[16]),
    .in5(in_1[15]), .in6(in_1[14]));
  not not_6 (out_3[16], xor_6_out);
  ExactlyOne xor_7 (
    .out(xor_7_out), .in0(in_1[13]), .in1(in_1[12]), .in2(in_1[11]), .in3(in_1[10]), .in4(in_1[9]),
    .in5(in_1[8]), .in6(in_1[7]));
  not not_7 (out_3[8], xor_7_out);
  ExactlyOne xor_8 (
    .out(xor_8_out), .in0(in_1[6]), .in1(in_1[5]), .in2(in_1[4]), .in3(in_1[3]), .in4(in_1[2]),
    .in5(in_1[1]), .in6(in_1[0]));
  not not_8 (out_3[0], xor_8_out);
  // Probe on {in_1[6], in_1[13], in_1[20], in_1[27], in_1[34], in_1[41], in_1[48], in_1[55], in_1[5], in_1[12], in_1[19], in_1[26], in_1[33], in_1[40], in_1[47], in_1[54], in_1[4], in_1[11], in_1[18], in_1[25], in_1[32], in_1[39], in_1[46], in_1[53], in_1[3], in_1[10], in_1[17], in_1[24]}
  // Probe on {in_1[0], in_1[7], in_1[14], in_1[21], in_1[28], in_1[35], in_1[42], in_1[49], in_1[1], in_1[8], in_1[15], in_1[22], in_1[29], in_1[36], in_1[43], in_1[50], in_1[2], in_1[9], in_1[16], in_1[23], in_1[30], in_1[37], in_1[44], in_1[51], in_1[31], in_1[38], in_1[45], in_1[52]}

  assign C = {in_1[6], in_1[13], in_1[20], in_1[27], in_1[34], in_1[41], in_1[48], in_1[55], in_1[5], in_1[12], in_1[19], in_1[26], in_1[33], in_1[40], in_1[47], in_1[54], in_1[4], in_1[11], in_1[18], in_1[25], in_1[32], in_1[39], in_1[46], in_1[53], in_1[3], in_1[10], in_1[17], in_1[24]};
  assign D = {in_1[0], in_1[7], in_1[14], in_1[21], in_1[28], in_1[35], in_1[42], in_1[49], in_1[1], in_1[8], in_1[15], in_1[22], in_1[29], in_1[36], in_1[43], in_1[50], in_1[2], in_1[9], in_1[16], in_1[23], in_1[30], in_1[37], in_1[44], in_1[51], in_1[31], in_1[38], in_1[45], in_1[52]};
  assign {out_3[63:57], out_3[55:49], out_3[47:41], out_3[39:33], out_3[31:25], out_3[23:17], out_3[15:9], out_3[7:1]} = in_1;

  // Other names for the same wires on the sheet: i36 = in_1[24]; i44 = in_1[17]; i52 = in_1[10]; i60 = in_1[3];
  //   i3 = in_1[53]; i11 = in_1[46]; i19 = in_1[39]; i27 = in_1[32]; i35 = in_1[25]; i43 = in_1[18]; i51 = in_1[11];
  //   i59 = in_1[4]; i2 = in_1[54]; i10 = in_1[47]; i18 = in_1[40]; i26 = in_1[33]; i34 = in_1[26]; i42 = in_1[19];
  //   i50 = in_1[12]; i58 = in_1[5]; i1 = in_1[55]; i9 = in_1[48]; i17 = in_1[41]; i25 = in_1[34]; i33 = in_1[27];
  //   i41 = in_1[20]; i49 = in_1[13]; i57 = in_1[6]; i4 = in_1[52]; i12 = in_1[45]; i20 = in_1[38]; i28 = in_1[31];
  //   i5 = in_1[51]; i13 = in_1[44]; i21 = in_1[37]; i29 = in_1[30]; i37 = in_1[23]; i45 = in_1[16]; i53 = in_1[9];
  //   i61 = in_1[2]; i6 = in_1[50]; i14 = in_1[43]; i22 = in_1[36]; i30 = in_1[29]; i38 = in_1[22]; i46 = in_1[15];
  //   i54 = in_1[8]; i62 = in_1[1]; i7 = in_1[49]; i15 = in_1[42]; i23 = in_1[35]; i31 = in_1[28]; i39 = in_1[21];
  //   i47 = in_1[14]; i55 = in_1[7]; i63 = in_1[0]; i64 = out_3[0]; i56 = out_3[8]; i48 = out_3[16]; i40 = out_3[24];
  //   i32 = out_3[32]; i24 = out_3[40]; i16 = out_3[48]; i8 = out_3[56]
endmodule

module shift_key1 (
  input  [27:0] in_1,
  output [27:0] out_2
);


  assign out_2 = {in_1[26:0], in_1[27]};
endmodule

module shift_key2 (
  input  [27:0] in_1,
  output [27:0] out_2
);


  assign out_2 = {in_1[25:0], in_1[27:26]};
endmodule

module S1 (
  input  [5:0] in_1,
  output [3:0] B8
);

  wire C0, C1, C2, C3, N0, N1, N2, N3, N4, N5, N6, N7, N8, N9, N10, N11, N12, N13, N14, N15, not_1_out,
       not_2_out, not_3_out, not_4_out;
  wire [3:0] eshkere_1_out_10, eshkere_2_out_10, eshkere_3_out_10, eshkere_4_out_10, eshkere_5_out_10,
       eshkere_6_out_10, eshkere_7_out_10, eshkere_8_out_10, eshkere_9_out_10, eshkere_10_out_10,
       eshkere_11_out_10, eshkere_12_out_10, eshkere_13_out_10, eshkere_14_out_10, eshkere_15_out_10,
       eshkere_16_out_10;

  not not_1 (not_1_out, in_1[5]);
  not not_2 (not_2_out, in_1[0]);
  not not_3 (not_3_out, in_1[0]);
  not not_4 (not_4_out, in_1[5]);
  and and_1 (C0, not_1_out, not_2_out);
  and and_2 (C2, in_1[5], not_3_out);
  and and_3 (C1, not_4_out, in_1[0]);
  and and_4 (C3, in_1[5], in_1[0]);
  and and_5 (N0, ~in_1[4], ~in_1[3], ~in_1[2], ~in_1[1]);  // AND_Gate
  and and_6 (N1, ~in_1[4], ~in_1[3], ~in_1[2], in_1[1]);  // AND_Gate
  and and_7 (N2, ~in_1[4], ~in_1[3], in_1[2], ~in_1[1]);  // AND_Gate
  and and_8 (N3, ~in_1[4], ~in_1[3], in_1[2], in_1[1]);  // AND_Gate
  and and_9 (N4, ~in_1[4], in_1[3], ~in_1[2], ~in_1[1]);  // AND_Gate
  and and_10 (N5, ~in_1[4], in_1[3], ~in_1[2], in_1[1]);  // AND_Gate
  and and_11 (N6, ~in_1[4], in_1[3], in_1[2], ~in_1[1]);  // AND_Gate
  and and_12 (N7, ~in_1[4], in_1[3], in_1[2], in_1[1]);  // AND_Gate
  and and_13 (N8, in_1[4], ~in_1[3], ~in_1[2], ~in_1[1]);  // AND_Gate
  and and_14 (N9, in_1[4], ~in_1[3], ~in_1[2], in_1[1]);  // AND_Gate
  and and_15 (N10, in_1[4], ~in_1[3], in_1[2], ~in_1[1]);  // AND_Gate
  and and_16 (N11, in_1[4], ~in_1[3], in_1[2], in_1[1]);  // AND_Gate
  and and_17 (N12, in_1[4], in_1[3], ~in_1[2], ~in_1[1]);  // AND_Gate
  and and_18 (N13, in_1[4], in_1[3], ~in_1[2], in_1[1]);  // AND_Gate
  and and_19 (N14, in_1[4], in_1[3], in_1[2], ~in_1[1]);  // AND_Gate
  and and_20 (N15, in_1[4], in_1[3], in_1[2], in_1[1]);
  Eshkere eshkere_1 (
    .N(N0), .C0(C0), .C1(C1), .C2(C2), .C3(C3), .E0(4'b1110), .E1(4'b0000), .E2(4'b0100), .E3(4'b1111),
    .out_10(eshkere_1_out_10));
  Eshkere eshkere_2 (
    .N(N1), .C0(C0), .C1(C1), .C2(C2), .C3(C3), .E0(4'b0100), .E1(4'b1111), .E2(4'b0001), .E3(4'b1100),
    .out_10(eshkere_2_out_10));
  Eshkere eshkere_3 (
    .N(N2), .C0(C0), .C1(C1), .C2(C2), .C3(C3), .E0(4'b1101), .E1(4'b0111), .E2(4'b1110), .E3(4'b1000),
    .out_10(eshkere_3_out_10));
  Eshkere eshkere_4 (
    .N(N3), .C0(C0), .C1(C1), .C2(C2), .C3(C3), .E0(4'b0001), .E1(4'b0100), .E2(4'b1000), .E3(4'b0010),
    .out_10(eshkere_4_out_10));
  Eshkere eshkere_5 (
    .N(N4), .C0(C0), .C1(C1), .C2(C2), .C3(C3), .E0(4'b0010), .E1(4'b1110), .E2(4'b1101), .E3(4'b0100),
    .out_10(eshkere_5_out_10));
  Eshkere eshkere_6 (
    .N(N5), .C0(C0), .C1(C1), .C2(C2), .C3(C3), .E0(4'b1111), .E1(4'b0010), .E2(4'b0110), .E3(4'b1001),
    .out_10(eshkere_6_out_10));
  Eshkere eshkere_7 (
    .N(N6), .C0(C0), .C1(C1), .C2(C2), .C3(C3), .E0(4'b1011), .E1(4'b1101), .E2(4'b0010), .E3(4'b0001),
    .out_10(eshkere_7_out_10));
  Eshkere eshkere_8 (
    .N(N7), .C0(C0), .C1(C1), .C2(C2), .C3(C3), .E0(4'b1000), .E1(4'b0001), .E2(4'b1011), .E3(4'b0111),
    .out_10(eshkere_8_out_10));
  Eshkere eshkere_9 (
    .N(N8), .C0(C0), .C1(C1), .C2(C2), .C3(C3), .E0(4'b0011), .E1(4'b1010), .E2(4'b1111), .E3(4'b0101),
    .out_10(eshkere_9_out_10));
  Eshkere eshkere_10 (
    .N(N9), .C0(C0), .C1(C1), .C2(C2), .C3(C3), .E0(4'b1010), .E1(4'b0110), .E2(4'b1100), .E3(4'b1011),
    .out_10(eshkere_10_out_10));
  Eshkere eshkere_11 (
    .N(N10), .C0(C0), .C1(C1), .C2(C2), .C3(C3), .E0(4'b0110), .E1(4'b1100), .E2(4'b1001), .E3(4'b0011),
    .out_10(eshkere_11_out_10));
  Eshkere eshkere_12 (
    .N(N11), .C0(C0), .C1(C1), .C2(C2), .C3(C3), .E0(4'b1100), .E1(4'b1011), .E2(4'b0111), .E3(4'b1110),
    .out_10(eshkere_12_out_10));
  Eshkere eshkere_13 (
    .N(N12), .C0(C0), .C1(C1), .C2(C2), .C3(C3), .E0(4'b0101), .E1(4'b1001), .E2(4'b0011), .E3(4'b1010),
    .out_10(eshkere_13_out_10));
  Eshkere eshkere_14 (
    .N(N13), .C0(C0), .C1(C1), .C2(C2), .C3(C3), .E0(4'b1001), .E1(4'b0101), .E2(4'b1010), .E3(4'b0000),
    .out_10(eshkere_14_out_10));
  Eshkere eshkere_15 (
    .N(N14), .C0(C0), .C1(C1), .C2(C2), .C3(C3), .E0(4'b0000), .E1(4'b0011), .E2(4'b0101), .E3(4'b0110),
    .out_10(eshkere_15_out_10));
  Eshkere eshkere_16 (
    .N(N15), .C0(C0), .C1(C1), .C2(C2), .C3(C3), .E0(4'b0111), .E1(4'b1000), .E2(4'b0000), .E3(4'b1101),
    .out_10(eshkere_16_out_10));
  assign B8 = eshkere_1_out_10 | eshkere_10_out_10 | eshkere_2_out_10 | eshkere_11_out_10 | eshkere_3_out_10 | eshkere_12_out_10 | eshkere_4_out_10 | eshkere_13_out_10 | eshkere_5_out_10 | eshkere_14_out_10 | eshkere_6_out_10 | eshkere_15_out_10 | eshkere_7_out_10 | eshkere_16_out_10 | eshkere_8_out_10 | eshkere_9_out_10;  // OR_Gate or_1, 4 bits wide

  // Other names for the same wires on the sheet: B2 = in_1[0]; M4 = in_1[1]; M3 = in_1[2]; M2 = in_1[3]; M1 = in_1[4];
  //   B1 = in_1[5]
endmodule

module S2 (
  input  [5:0] in_1,
  output [3:0] B8
);

  wire C0, C1, C2, C3, N0, N1, N2, N3, N4, N5, N6, N7, N8, N9, N10, N11, N12, N13, N14, N15, not_1_out,
       not_2_out, not_3_out, not_4_out;
  wire [3:0] eshkere_1_out_10, eshkere_2_out_10, eshkere_3_out_10, eshkere_4_out_10, eshkere_5_out_10,
       eshkere_6_out_10, eshkere_7_out_10, eshkere_8_out_10, eshkere_9_out_10, eshkere_10_out_10,
       eshkere_11_out_10, eshkere_12_out_10, eshkere_13_out_10, eshkere_14_out_10, eshkere_15_out_10,
       eshkere_16_out_10;

  not not_1 (not_1_out, in_1[5]);
  and and_1 (C0, not_1_out, not_2_out);
  not not_2 (not_2_out, in_1[0]);
  and and_2 (C2, in_1[5], not_3_out);
  not not_3 (not_3_out, in_1[0]);
  not not_4 (not_4_out, in_1[5]);
  and and_3 (C1, not_4_out, in_1[0]);
  and and_4 (C3, in_1[5], in_1[0]);
  and and_5 (N0, ~in_1[4], ~in_1[3], ~in_1[2], ~in_1[1]);  // AND_Gate
  and and_6 (N1, ~in_1[4], ~in_1[3], ~in_1[2], in_1[1]);  // AND_Gate
  and and_7 (N2, ~in_1[4], ~in_1[3], in_1[2], ~in_1[1]);  // AND_Gate
  and and_8 (N3, ~in_1[4], ~in_1[3], in_1[2], in_1[1]);  // AND_Gate
  and and_9 (N4, ~in_1[4], in_1[3], ~in_1[2], ~in_1[1]);  // AND_Gate
  and and_10 (N5, ~in_1[4], in_1[3], ~in_1[2], in_1[1]);  // AND_Gate
  and and_11 (N6, ~in_1[4], in_1[3], in_1[2], ~in_1[1]);  // AND_Gate
  and and_12 (N7, ~in_1[4], in_1[3], in_1[2], in_1[1]);  // AND_Gate
  and and_13 (N8, in_1[4], ~in_1[3], ~in_1[2], ~in_1[1]);  // AND_Gate
  and and_14 (N9, in_1[4], ~in_1[3], ~in_1[2], in_1[1]);  // AND_Gate
  and and_15 (N10, in_1[4], ~in_1[3], in_1[2], ~in_1[1]);  // AND_Gate
  and and_16 (N11, in_1[4], ~in_1[3], in_1[2], in_1[1]);  // AND_Gate
  and and_17 (N12, in_1[4], in_1[3], ~in_1[2], ~in_1[1]);  // AND_Gate
  and and_18 (N13, in_1[4], in_1[3], ~in_1[2], in_1[1]);  // AND_Gate
  and and_19 (N14, in_1[4], in_1[3], in_1[2], ~in_1[1]);  // AND_Gate
  and and_20 (N15, in_1[4], in_1[3], in_1[2], in_1[1]);
  Eshkere eshkere_1 (
    .N(N0), .C0(C0), .C1(C1), .C2(C2), .C3(C3), .E0(4'b1111), .E1(4'b0011), .E2(4'b0000), .E3(4'b1101),
    .out_10(eshkere_1_out_10));
  Eshkere eshkere_2 (
    .N(N1), .C0(C0), .C1(C1), .C2(C2), .C3(C3), .E0(4'b0001), .E1(4'b1101), .E2(4'b1110), .E3(4'b1000),
    .out_10(eshkere_2_out_10));
  Eshkere eshkere_3 (
    .N(N2), .C0(C0), .C1(C1), .C2(C2), .C3(C3), .E0(4'b1000), .E1(4'b0100), .E2(4'b0111), .E3(4'b1010),
    .out_10(eshkere_3_out_10));
  Eshkere eshkere_4 (
    .N(N3), .C0(C0), .C1(C1), .C2(C2), .C3(C3), .E0(4'b1110), .E1(4'b0111), .E2(4'b1011), .E3(4'b0001),
    .out_10(eshkere_4_out_10));
  Eshkere eshkere_5 (
    .N(N4), .C0(C0), .C1(C1), .C2(C2), .C3(C3), .E0(4'b0110), .E1(4'b1111), .E2(4'b1010), .E3(4'b0011),
    .out_10(eshkere_5_out_10));
  Eshkere eshkere_6 (
    .N(N5), .C0(C0), .C1(C1), .C2(C2), .C3(C3), .E0(4'b1011), .E1(4'b0010), .E2(4'b0100), .E3(4'b1111),
    .out_10(eshkere_6_out_10));
  Eshkere eshkere_7 (
    .N(N6), .C0(C0), .C1(C1), .C2(C2), .C3(C3), .E0(4'b0011), .E1(4'b1000), .E2(4'b1101), .E3(4'b0100),
    .out_10(eshkere_7_out_10));
  Eshkere eshkere_8 (
    .N(N7), .C0(C0), .C1(C1), .C2(C2), .C3(C3), .E0(4'b0100), .E1(4'b1110), .E2(4'b0001), .E3(4'b0010),
    .out_10(eshkere_8_out_10));
  Eshkere eshkere_9 (
    .N(N8), .C0(C0), .C1(C1), .C2(C2), .C3(C3), .E0(4'b1001), .E1(4'b1100), .E2(4'b0101), .E3(4'b1011),
    .out_10(eshkere_9_out_10));
  Eshkere eshkere_10 (
    .N(N9), .C0(C0), .C1(C1), .C2(C2), .C3(C3), .E0(4'b0111), .E1(4'b0000), .E2(4'b1000), .E3(4'b0110),
    .out_10(eshkere_10_out_10));
  Eshkere eshkere_11 (
    .N(N10), .C0(C0), .C1(C1), .C2(C2), .C3(C3), .E0(4'b0010), .E1(4'b0001), .E2(4'b1100), .E3(4'b0111),
    .out_10(eshkere_11_out_10));
  Eshkere eshkere_12 (
    .N(N11), .C0(C0), .C1(C1), .C2(C2), .C3(C3), .E0(4'b1101), .E1(4'b1010), .E2(4'b0110), .E3(4'b1100),
    .out_10(eshkere_12_out_10));
  Eshkere eshkere_13 (
    .N(N12), .C0(C0), .C1(C1), .C2(C2), .C3(C3), .E0(4'b1100), .E1(4'b0110), .E2(4'b1001), .E3(4'b0000),
    .out_10(eshkere_13_out_10));
  Eshkere eshkere_14 (
    .N(N13), .C0(C0), .C1(C1), .C2(C2), .C3(C3), .E0(4'b0000), .E1(4'b1001), .E2(4'b0011), .E3(4'b0101),
    .out_10(eshkere_14_out_10));
  Eshkere eshkere_15 (
    .N(N14), .C0(C0), .C1(C1), .C2(C2), .C3(C3), .E0(4'b0101), .E1(4'b1011), .E2(4'b0010), .E3(4'b1110),
    .out_10(eshkere_15_out_10));
  Eshkere eshkere_16 (
    .N(N15), .C0(C0), .C1(C1), .C2(C2), .C3(C3), .E0(4'b1010), .E1(4'b0101), .E2(4'b1111), .E3(4'b1001),
    .out_10(eshkere_16_out_10));
  assign B8 = eshkere_1_out_10 | eshkere_10_out_10 | eshkere_2_out_10 | eshkere_11_out_10 | eshkere_3_out_10 | eshkere_12_out_10 | eshkere_4_out_10 | eshkere_13_out_10 | eshkere_5_out_10 | eshkere_14_out_10 | eshkere_6_out_10 | eshkere_15_out_10 | eshkere_7_out_10 | eshkere_16_out_10 | eshkere_8_out_10 | eshkere_9_out_10;  // OR_Gate or_1, 4 bits wide

  // Other names for the same wires on the sheet: B2 = in_1[0]; M4 = in_1[1]; M3 = in_1[2]; M2 = in_1[3]; M1 = in_1[4];
  //   B1 = in_1[5]
endmodule

module S3 (
  input  [5:0] in_1,
  output [3:0] B8
);

  wire C0, C1, C2, C3, N0, N1, N2, N3, N4, N5, N6, N7, N8, N9, N10, N11, N12, N13, N14, N15, not_1_out,
       not_2_out, not_3_out, not_4_out;
  wire [3:0] eshkere_1_out_10, eshkere_2_out_10, eshkere_3_out_10, eshkere_4_out_10, eshkere_5_out_10,
       eshkere_6_out_10, eshkere_7_out_10, eshkere_8_out_10, eshkere_9_out_10, eshkere_10_out_10,
       eshkere_11_out_10, eshkere_12_out_10, eshkere_13_out_10, eshkere_14_out_10, eshkere_15_out_10,
       eshkere_16_out_10;

  not not_1 (not_1_out, in_1[5]);
  not not_2 (not_2_out, in_1[0]);
  not not_3 (not_3_out, in_1[0]);
  not not_4 (not_4_out, in_1[5]);
  and and_1 (C0, not_1_out, not_2_out);
  and and_2 (C2, in_1[5], not_3_out);
  and and_3 (C1, not_4_out, in_1[0]);
  and and_4 (C3, in_1[5], in_1[0]);
  and and_5 (N0, ~in_1[4], ~in_1[3], ~in_1[2], ~in_1[1]);  // AND_Gate
  and and_6 (N1, ~in_1[4], ~in_1[3], ~in_1[2], in_1[1]);  // AND_Gate
  and and_7 (N2, ~in_1[4], ~in_1[3], in_1[2], ~in_1[1]);  // AND_Gate
  and and_8 (N3, ~in_1[4], ~in_1[3], in_1[2], in_1[1]);  // AND_Gate
  and and_9 (N4, ~in_1[4], in_1[3], ~in_1[2], ~in_1[1]);  // AND_Gate
  and and_10 (N5, ~in_1[4], in_1[3], ~in_1[2], in_1[1]);  // AND_Gate
  and and_11 (N6, ~in_1[4], in_1[3], in_1[2], ~in_1[1]);  // AND_Gate
  and and_12 (N7, ~in_1[4], in_1[3], in_1[2], in_1[1]);  // AND_Gate
  and and_13 (N8, in_1[4], ~in_1[3], ~in_1[2], ~in_1[1]);  // AND_Gate
  and and_14 (N9, in_1[4], ~in_1[3], ~in_1[2], in_1[1]);  // AND_Gate
  and and_15 (N10, in_1[4], ~in_1[3], in_1[2], ~in_1[1]);  // AND_Gate
  and and_16 (N11, in_1[4], ~in_1[3], in_1[2], in_1[1]);  // AND_Gate
  and and_17 (N12, in_1[4], in_1[3], ~in_1[2], ~in_1[1]);  // AND_Gate
  and and_18 (N13, in_1[4], in_1[3], ~in_1[2], in_1[1]);  // AND_Gate
  and and_19 (N14, in_1[4], in_1[3], in_1[2], ~in_1[1]);  // AND_Gate
  and and_20 (N15, in_1[4], in_1[3], in_1[2], in_1[1]);
  Eshkere eshkere_1 (
    .N(N0), .C0(C0), .C1(C1), .C2(C2), .C3(C3), .E0(4'b1010), .E1(4'b1101), .E2(4'b1101), .E3(4'b0001),
    .out_10(eshkere_1_out_10));
  Eshkere eshkere_2 (
    .N(N1), .C0(C0), .C1(C1), .C2(C2), .C3(C3), .E0(4'b0000), .E1(4'b0111), .E2(4'b0110), .E3(4'b1010),
    .out_10(eshkere_2_out_10));
  Eshkere eshkere_3 (
    .N(N2), .C0(C0), .C1(C1), .C2(C2), .C3(C3), .E0(4'b1001), .E1(4'b0000), .E2(4'b0100), .E3(4'b1101),
    .out_10(eshkere_3_out_10));
  Eshkere eshkere_4 (
    .N(N3), .C0(C0), .C1(C1), .C2(C2), .C3(C3), .E0(4'b1110), .E1(4'b1001), .E2(4'b1001), .E3(4'b0000),
    .out_10(eshkere_4_out_10));
  Eshkere eshkere_5 (
    .N(N4), .C0(C0), .C1(C1), .C2(C2), .C3(C3), .E0(4'b0110), .E1(4'b0011), .E2(4'b1000), .E3(4'b0110),
    .out_10(eshkere_5_out_10));
  Eshkere eshkere_6 (
    .N(N5), .C0(C0), .C1(C1), .C2(C2), .C3(C3), .E0(4'b0011), .E1(4'b0100), .E2(4'b1111), .E3(4'b1001),
    .out_10(eshkere_6_out_10));
  Eshkere eshkere_7 (
    .N(N6), .C0(C0), .C1(C1), .C2(C2), .C3(C3), .E0(4'b1111), .E1(4'b0110), .E2(4'b0011), .E3(4'b1000),
    .out_10(eshkere_7_out_10));
  Eshkere eshkere_8 (
    .N(N7), .C0(C0), .C1(C1), .C2(C2), .C3(C3), .E0(4'b0101), .E1(4'b1010), .E2(4'b0000), .E3(4'b0111),
    .out_10(eshkere_8_out_10));
  Eshkere eshkere_9 (
    .N(N8), .C0(C0), .C1(C1), .C2(C2), .C3(C3), .E0(4'b0001), .E1(4'b0010), .E2(4'b1011), .E3(4'b0100),
    .out_10(eshkere_9_out_10));
  Eshkere eshkere_10 (
    .N(N9), .C0(C0), .C1(C1), .C2(C2), .C3(C3), .E0(4'b1101), .E1(4'b1000), .E2(4'b0001), .E3(4'b1111),
    .out_10(eshkere_10_out_10));
  Eshkere eshkere_11 (
    .N(N10), .C0(C0), .C1(C1), .C2(C2), .C3(C3), .E0(4'b1100), .E1(4'b0101), .E2(4'b0010), .E3(4'b1110),
    .out_10(eshkere_11_out_10));
  Eshkere eshkere_12 (
    .N(N11), .C0(C0), .C1(C1), .C2(C2), .C3(C3), .E0(4'b0111), .E1(4'b1110), .E2(4'b1100), .E3(4'b0011),
    .out_10(eshkere_12_out_10));
  Eshkere eshkere_13 (
    .N(N12), .C0(C0), .C1(C1), .C2(C2), .C3(C3), .E0(4'b1011), .E1(4'b1100), .E2(4'b0101), .E3(4'b1011),
    .out_10(eshkere_13_out_10));
  Eshkere eshkere_14 (
    .N(N13), .C0(C0), .C1(C1), .C2(C2), .C3(C3), .E0(4'b0100), .E1(4'b1011), .E2(4'b1010), .E3(4'b0101),
    .out_10(eshkere_14_out_10));
  Eshkere eshkere_15 (
    .N(N14), .C0(C0), .C1(C1), .C2(C2), .C3(C3), .E0(4'b0010), .E1(4'b1111), .E2(4'b1110), .E3(4'b0010),
    .out_10(eshkere_15_out_10));
  Eshkere eshkere_16 (
    .N(N15), .C0(C0), .C1(C1), .C2(C2), .C3(C3), .E0(4'b1000), .E1(4'b0001), .E2(4'b0111), .E3(4'b1100),
    .out_10(eshkere_16_out_10));
  assign B8 = eshkere_1_out_10 | eshkere_10_out_10 | eshkere_2_out_10 | eshkere_11_out_10 | eshkere_3_out_10 | eshkere_12_out_10 | eshkere_4_out_10 | eshkere_13_out_10 | eshkere_5_out_10 | eshkere_14_out_10 | eshkere_6_out_10 | eshkere_15_out_10 | eshkere_7_out_10 | eshkere_16_out_10 | eshkere_8_out_10 | eshkere_9_out_10;  // OR_Gate or_1, 4 bits wide

  // Other names for the same wires on the sheet: B2 = in_1[0]; M4 = in_1[1]; M3 = in_1[2]; M2 = in_1[3]; M1 = in_1[4];
  //   B1 = in_1[5]
endmodule

module S4 (
  input  [5:0] in_1,
  output [3:0] B8
);

  wire C0, C1, C2, C3, N0, N1, N2, N3, N4, N5, N6, N7, N8, N9, N10, N11, N12, N13, N14, N15, not_1_out,
       not_2_out, not_3_out, not_4_out;
  wire [3:0] eshkere_1_out_10, eshkere_2_out_10, eshkere_3_out_10, eshkere_4_out_10, eshkere_5_out_10,
       eshkere_6_out_10, eshkere_7_out_10, eshkere_8_out_10, eshkere_9_out_10, eshkere_10_out_10,
       eshkere_11_out_10, eshkere_12_out_10, eshkere_13_out_10, eshkere_14_out_10, eshkere_15_out_10,
       eshkere_16_out_10;

  not not_1 (not_1_out, in_1[5]);
  and and_1 (C0, not_1_out, not_2_out);
  not not_2 (not_2_out, in_1[0]);
  and and_2 (C2, in_1[5], not_3_out);
  not not_3 (not_3_out, in_1[0]);
  not not_4 (not_4_out, in_1[5]);
  and and_3 (C1, not_4_out, in_1[0]);
  and and_4 (C3, in_1[5], in_1[0]);
  and and_5 (N0, ~in_1[4], ~in_1[3], ~in_1[2], ~in_1[1]);  // AND_Gate
  and and_6 (N1, ~in_1[4], ~in_1[3], ~in_1[2], in_1[1]);  // AND_Gate
  and and_7 (N2, ~in_1[4], ~in_1[3], in_1[2], ~in_1[1]);  // AND_Gate
  and and_8 (N3, ~in_1[4], ~in_1[3], in_1[2], in_1[1]);  // AND_Gate
  and and_9 (N4, ~in_1[4], in_1[3], ~in_1[2], ~in_1[1]);  // AND_Gate
  and and_10 (N5, ~in_1[4], in_1[3], ~in_1[2], in_1[1]);  // AND_Gate
  and and_11 (N6, ~in_1[4], in_1[3], in_1[2], ~in_1[1]);  // AND_Gate
  and and_12 (N7, ~in_1[4], in_1[3], in_1[2], in_1[1]);  // AND_Gate
  and and_13 (N8, in_1[4], ~in_1[3], ~in_1[2], ~in_1[1]);  // AND_Gate
  and and_14 (N9, in_1[4], ~in_1[3], ~in_1[2], in_1[1]);  // AND_Gate
  and and_15 (N10, in_1[4], ~in_1[3], in_1[2], ~in_1[1]);  // AND_Gate
  and and_16 (N11, in_1[4], ~in_1[3], in_1[2], in_1[1]);  // AND_Gate
  and and_17 (N12, in_1[4], in_1[3], ~in_1[2], ~in_1[1]);  // AND_Gate
  and and_18 (N13, in_1[4], in_1[3], ~in_1[2], in_1[1]);  // AND_Gate
  and and_19 (N14, in_1[4], in_1[3], in_1[2], ~in_1[1]);  // AND_Gate
  and and_20 (N15, in_1[4], in_1[3], in_1[2], in_1[1]);
  Eshkere eshkere_1 (
    .N(N0), .C0(C0), .C1(C1), .C2(C2), .C3(C3), .E0(4'b0111), .E1(4'b1101), .E2(4'b1010), .E3(4'b0011),
    .out_10(eshkere_1_out_10));
  Eshkere eshkere_2 (
    .N(N1), .C0(C0), .C1(C1), .C2(C2), .C3(C3), .E0(4'b1101), .E1(4'b1000), .E2(4'b0110), .E3(4'b1111),
    .out_10(eshkere_2_out_10));
  Eshkere eshkere_3 (
    .N(N2), .C0(C0), .C1(C1), .C2(C2), .C3(C3), .E0(4'b1110), .E1(4'b1011), .E2(4'b1001), .E3(4'b0000),
    .out_10(eshkere_3_out_10));
  Eshkere eshkere_4 (
    .N(N3), .C0(C0), .C1(C1), .C2(C2), .C3(C3), .E0(4'b0011), .E1(4'b0101), .E2(4'b0000), .E3(4'b0110),
    .out_10(eshkere_4_out_10));
  Eshkere eshkere_5 (
    .N(N4), .C0(C0), .C1(C1), .C2(C2), .C3(C3), .E0(4'b0000), .E1(4'b0110), .E2(4'b1100), .E3(4'b1010),
    .out_10(eshkere_5_out_10));
  Eshkere eshkere_6 (
    .N(N5), .C0(C0), .C1(C1), .C2(C2), .C3(C3), .E0(4'b0110), .E1(4'b1111), .E2(4'b1011), .E3(4'b0001),
    .out_10(eshkere_6_out_10));
  Eshkere eshkere_7 (
    .N(N6), .C0(C0), .C1(C1), .C2(C2), .C3(C3), .E0(4'b1001), .E1(4'b0000), .E2(4'b0111), .E3(4'b1101),
    .out_10(eshkere_7_out_10));
  Eshkere eshkere_8 (
    .N(N7), .C0(C0), .C1(C1), .C2(C2), .C3(C3), .E0(4'b1010), .E1(4'b0011), .E2(4'b1101), .E3(4'b1000),
    .out_10(eshkere_8_out_10));
  Eshkere eshkere_9 (
    .N(N8), .C0(C0), .C1(C1), .C2(C2), .C3(C3), .E0(4'b0001), .E1(4'b0100), .E2(4'b1111), .E3(4'b1001),
    .out_10(eshkere_9_out_10));
  Eshkere eshkere_10 (
    .N(N9), .C0(C0), .C1(C1), .C2(C2), .C3(C3), .E0(4'b0010), .E1(4'b0111), .E2(4'b0001), .E3(4'b0100),
    .out_10(eshkere_10_out_10));
  Eshkere eshkere_11 (
    .N(N10), .C0(C0), .C1(C1), .C2(C2), .C3(C3), .E0(4'b1000), .E1(4'b0010), .E2(4'b0011), .E3(4'b0101),
    .out_10(eshkere_11_out_10));
  Eshkere eshkere_12 (
    .N(N11), .C0(C0), .C1(C1), .C2(C2), .C3(C3), .E0(4'b0101), .E1(4'b1100), .E2(4'b1110), .E3(4'b1011),
    .out_10(eshkere_12_out_10));
  Eshkere eshkere_13 (
    .N(N12), .C0(C0), .C1(C1), .C2(C2), .C3(C3), .E0(4'b1011), .E1(4'b0001), .E2(4'b0101), .E3(4'b1100),
    .out_10(eshkere_13_out_10));
  Eshkere eshkere_14 (
    .N(N13), .C0(C0), .C1(C1), .C2(C2), .C3(C3), .E0(4'b1100), .E1(4'b1010), .E2(4'b0010), .E3(4'b0111),
    .out_10(eshkere_14_out_10));
  Eshkere eshkere_15 (
    .N(N14), .C0(C0), .C1(C1), .C2(C2), .C3(C3), .E0(4'b0100), .E1(4'b1110), .E2(4'b1000), .E3(4'b0010),
    .out_10(eshkere_15_out_10));
  Eshkere eshkere_16 (
    .N(N15), .C0(C0), .C1(C1), .C2(C2), .C3(C3), .E0(4'b1111), .E1(4'b1001), .E2(4'b0100), .E3(4'b1110),
    .out_10(eshkere_16_out_10));
  assign B8 = eshkere_1_out_10 | eshkere_10_out_10 | eshkere_2_out_10 | eshkere_11_out_10 | eshkere_3_out_10 | eshkere_12_out_10 | eshkere_4_out_10 | eshkere_13_out_10 | eshkere_5_out_10 | eshkere_14_out_10 | eshkere_6_out_10 | eshkere_15_out_10 | eshkere_7_out_10 | eshkere_16_out_10 | eshkere_8_out_10 | eshkere_9_out_10;  // OR_Gate or_1, 4 bits wide

  // Other names for the same wires on the sheet: B2 = in_1[0]; M4 = in_1[1]; M3 = in_1[2]; M2 = in_1[3]; M1 = in_1[4];
  //   B1 = in_1[5]
endmodule

module S5 (
  input  [5:0] in_1,
  output [3:0] B8
);

  wire C0, C1, C2, C3, N0, N1, N2, N3, N4, N5, N6, N7, N8, N9, N10, N11, N12, N13, N14, N15, not_1_out,
       not_2_out, not_3_out, not_4_out;
  wire [3:0] eshkere_1_out_10, eshkere_2_out_10, eshkere_3_out_10, eshkere_4_out_10, eshkere_5_out_10,
       eshkere_6_out_10, eshkere_7_out_10, eshkere_8_out_10, eshkere_9_out_10, eshkere_10_out_10,
       eshkere_11_out_10, eshkere_12_out_10, eshkere_13_out_10, eshkere_14_out_10, eshkere_15_out_10,
       eshkere_16_out_10;

  not not_1 (not_1_out, in_1[5]);
  and and_1 (C0, not_1_out, not_2_out);
  not not_2 (not_2_out, in_1[0]);
  and and_2 (C2, in_1[5], not_3_out);
  not not_3 (not_3_out, in_1[0]);
  not not_4 (not_4_out, in_1[5]);
  and and_3 (C1, not_4_out, in_1[0]);
  and and_4 (C3, in_1[5], in_1[0]);
  and and_5 (N0, ~in_1[4], ~in_1[3], ~in_1[2], ~in_1[1]);  // AND_Gate
  and and_6 (N1, ~in_1[4], ~in_1[3], ~in_1[2], in_1[1]);  // AND_Gate
  and and_7 (N2, ~in_1[4], ~in_1[3], in_1[2], ~in_1[1]);  // AND_Gate
  and and_8 (N3, ~in_1[4], ~in_1[3], in_1[2], in_1[1]);  // AND_Gate
  and and_9 (N4, ~in_1[4], in_1[3], ~in_1[2], ~in_1[1]);  // AND_Gate
  and and_10 (N5, ~in_1[4], in_1[3], ~in_1[2], in_1[1]);  // AND_Gate
  and and_11 (N6, ~in_1[4], in_1[3], in_1[2], ~in_1[1]);  // AND_Gate
  and and_12 (N7, ~in_1[4], in_1[3], in_1[2], in_1[1]);  // AND_Gate
  and and_13 (N8, in_1[4], ~in_1[3], ~in_1[2], ~in_1[1]);  // AND_Gate
  and and_14 (N9, in_1[4], ~in_1[3], ~in_1[2], in_1[1]);  // AND_Gate
  and and_15 (N10, in_1[4], ~in_1[3], in_1[2], ~in_1[1]);  // AND_Gate
  and and_16 (N11, in_1[4], ~in_1[3], in_1[2], in_1[1]);  // AND_Gate
  and and_17 (N12, in_1[4], in_1[3], ~in_1[2], ~in_1[1]);  // AND_Gate
  and and_18 (N13, in_1[4], in_1[3], ~in_1[2], in_1[1]);  // AND_Gate
  and and_19 (N14, in_1[4], in_1[3], in_1[2], ~in_1[1]);  // AND_Gate
  and and_20 (N15, in_1[4], in_1[3], in_1[2], in_1[1]);
  Eshkere eshkere_1 (
    .N(N0), .C0(C0), .C1(C1), .C2(C2), .C3(C3), .E0(4'b0010), .E1(4'b1110), .E2(4'b0100), .E3(4'b1011),
    .out_10(eshkere_1_out_10));
  Eshkere eshkere_2 (
    .N(N1), .C0(C0), .C1(C1), .C2(C2), .C3(C3), .E0(4'b1100), .E1(4'b1011), .E2(4'b0010), .E3(4'b1000),
    .out_10(eshkere_2_out_10));
  Eshkere eshkere_3 (
    .N(N2), .C0(C0), .C1(C1), .C2(C2), .C3(C3), .E0(4'b0100), .E1(4'b0010), .E2(4'b0001), .E3(4'b1100),
    .out_10(eshkere_3_out_10));
  Eshkere eshkere_4 (
    .N(N3), .C0(C0), .C1(C1), .C2(C2), .C3(C3), .E0(4'b0001), .E1(4'b1100), .E2(4'b1011), .E3(4'b0111),
    .out_10(eshkere_4_out_10));
  Eshkere eshkere_5 (
    .N(N4), .C0(C0), .C1(C1), .C2(C2), .C3(C3), .E0(4'b0111), .E1(4'b0100), .E2(4'b1010), .E3(4'b0001),
    .out_10(eshkere_5_out_10));
  Eshkere eshkere_6 (
    .N(N5), .C0(C0), .C1(C1), .C2(C2), .C3(C3), .E0(4'b1010), .E1(4'b0111), .E2(4'b1101), .E3(4'b1110),
    .out_10(eshkere_6_out_10));
  Eshkere eshkere_7 (
    .N(N6), .C0(C0), .C1(C1), .C2(C2), .C3(C3), .E0(4'b1011), .E1(4'b1101), .E2(4'b0111), .E3(4'b0010),
    .out_10(eshkere_7_out_10));
  Eshkere eshkere_8 (
    .N(N7), .C0(C0), .C1(C1), .C2(C2), .C3(C3), .E0(4'b0110), .E1(4'b0001), .E2(4'b1000), .E3(4'b1101),
    .out_10(eshkere_8_out_10));
  Eshkere eshkere_9 (
    .N(N8), .C0(C0), .C1(C1), .C2(C2), .C3(C3), .E0(4'b1000), .E1(4'b0101), .E2(4'b1111), .E3(4'b0110),
    .out_10(eshkere_9_out_10));
  Eshkere eshkere_10 (
    .N(N9), .C0(C0), .C1(C1), .C2(C2), .C3(C3), .E0(4'b0101), .E1(4'b0000), .E2(4'b1001), .E3(4'b1111),
    .out_10(eshkere_10_out_10));
  Eshkere eshkere_11 (
    .N(N10), .C0(C0), .C1(C1), .C2(C2), .C3(C3), .E0(4'b0011), .E1(4'b1111), .E2(4'b1100), .E3(4'b0000),
    .out_10(eshkere_11_out_10));
  Eshkere eshkere_12 (
    .N(N11), .C0(C0), .C1(C1), .C2(C2), .C3(C3), .E0(4'b1111), .E1(4'b1010), .E2(4'b0101), .E3(4'b1001),
    .out_10(eshkere_12_out_10));
  Eshkere eshkere_13 (
    .N(N12), .C0(C0), .C1(C1), .C2(C2), .C3(C3), .E0(4'b1101), .E1(4'b0011), .E2(4'b0110), .E3(4'b1010),
    .out_10(eshkere_13_out_10));
  Eshkere eshkere_14 (
    .N(N13), .C0(C0), .C1(C1), .C2(C2), .C3(C3), .E0(4'b0000), .E1(4'b1001), .E2(4'b0011), .E3(4'b0100),
    .out_10(eshkere_14_out_10));
  Eshkere eshkere_15 (
    .N(N14), .C0(C0), .C1(C1), .C2(C2), .C3(C3), .E0(4'b1110), .E1(4'b1000), .E2(4'b0000), .E3(4'b0101),
    .out_10(eshkere_15_out_10));
  Eshkere eshkere_16 (
    .N(N15), .C0(C0), .C1(C1), .C2(C2), .C3(C3), .E0(4'b1001), .E1(4'b0110), .E2(4'b1110), .E3(4'b0011),
    .out_10(eshkere_16_out_10));
  assign B8 = eshkere_1_out_10 | eshkere_10_out_10 | eshkere_2_out_10 | eshkere_11_out_10 | eshkere_3_out_10 | eshkere_12_out_10 | eshkere_4_out_10 | eshkere_13_out_10 | eshkere_5_out_10 | eshkere_14_out_10 | eshkere_6_out_10 | eshkere_15_out_10 | eshkere_7_out_10 | eshkere_16_out_10 | eshkere_8_out_10 | eshkere_9_out_10;  // OR_Gate or_1, 4 bits wide

  // Other names for the same wires on the sheet: B2 = in_1[0]; M4 = in_1[1]; M3 = in_1[2]; M2 = in_1[3]; M1 = in_1[4];
  //   B1 = in_1[5]
endmodule

module S6 (
  input  [5:0] in_1,
  output [3:0] B8
);

  wire C0, C1, C2, C3, N0, N1, N2, N3, N4, N5, N6, N7, N8, N9, N10, N11, N12, N13, N14, N15, not_1_out,
       not_2_out, not_3_out, not_4_out;
  wire [3:0] eshkere_1_out_10, eshkere_2_out_10, eshkere_3_out_10, eshkere_4_out_10, eshkere_5_out_10,
       eshkere_6_out_10, eshkere_7_out_10, eshkere_8_out_10, eshkere_9_out_10, eshkere_10_out_10,
       eshkere_11_out_10, eshkere_12_out_10, eshkere_13_out_10, eshkere_14_out_10, eshkere_15_out_10,
       eshkere_16_out_10;

  not not_1 (not_1_out, in_1[5]);
  and and_1 (C0, not_1_out, not_2_out);
  not not_2 (not_2_out, in_1[0]);
  and and_2 (C2, in_1[5], not_3_out);
  not not_3 (not_3_out, in_1[0]);
  not not_4 (not_4_out, in_1[5]);
  and and_3 (C1, not_4_out, in_1[0]);
  and and_4 (C3, in_1[5], in_1[0]);
  and and_5 (N0, ~in_1[4], ~in_1[3], ~in_1[2], ~in_1[1]);  // AND_Gate
  and and_6 (N1, ~in_1[4], ~in_1[3], ~in_1[2], in_1[1]);  // AND_Gate
  and and_7 (N2, ~in_1[4], ~in_1[3], in_1[2], ~in_1[1]);  // AND_Gate
  and and_8 (N3, ~in_1[4], ~in_1[3], in_1[2], in_1[1]);  // AND_Gate
  and and_9 (N4, ~in_1[4], in_1[3], ~in_1[2], ~in_1[1]);  // AND_Gate
  and and_10 (N5, ~in_1[4], in_1[3], ~in_1[2], in_1[1]);  // AND_Gate
  and and_11 (N6, ~in_1[4], in_1[3], in_1[2], ~in_1[1]);  // AND_Gate
  and and_12 (N7, ~in_1[4], in_1[3], in_1[2], in_1[1]);  // AND_Gate
  and and_13 (N8, in_1[4], ~in_1[3], ~in_1[2], ~in_1[1]);  // AND_Gate
  and and_14 (N9, in_1[4], ~in_1[3], ~in_1[2], in_1[1]);  // AND_Gate
  and and_15 (N10, in_1[4], ~in_1[3], in_1[2], ~in_1[1]);  // AND_Gate
  and and_16 (N11, in_1[4], ~in_1[3], in_1[2], in_1[1]);  // AND_Gate
  and and_17 (N12, in_1[4], in_1[3], ~in_1[2], ~in_1[1]);  // AND_Gate
  and and_18 (N13, in_1[4], in_1[3], ~in_1[2], in_1[1]);  // AND_Gate
  and and_19 (N14, in_1[4], in_1[3], in_1[2], ~in_1[1]);  // AND_Gate
  and and_20 (N15, in_1[4], in_1[3], in_1[2], in_1[1]);
  Eshkere eshkere_1 (
    .N(N0), .C0(C0), .C1(C1), .C2(C2), .C3(C3), .E0(4'b1100), .E1(4'b1010), .E2(4'b1001), .E3(4'b0100),
    .out_10(eshkere_1_out_10));
  Eshkere eshkere_2 (
    .N(N1), .C0(C0), .C1(C1), .C2(C2), .C3(C3), .E0(4'b0001), .E1(4'b1111), .E2(4'b1110), .E3(4'b0011),
    .out_10(eshkere_2_out_10));
  Eshkere eshkere_3 (
    .N(N2), .C0(C0), .C1(C1), .C2(C2), .C3(C3), .E0(4'b1010), .E1(4'b0100), .E2(4'b1111), .E3(4'b0010),
    .out_10(eshkere_3_out_10));
  Eshkere eshkere_4 (
    .N(N3), .C0(C0), .C1(C1), .C2(C2), .C3(C3), .E0(4'b1111), .E1(4'b0010), .E2(4'b0101), .E3(4'b1100),
    .out_10(eshkere_4_out_10));
  Eshkere eshkere_5 (
    .N(N4), .C0(C0), .C1(C1), .C2(C2), .C3(C3), .E0(4'b1001), .E1(4'b0111), .E2(4'b0010), .E3(4'b1001),
    .out_10(eshkere_5_out_10));
  Eshkere eshkere_6 (
    .N(N5), .C0(C0), .C1(C1), .C2(C2), .C3(C3), .E0(4'b0010), .E1(4'b1100), .E2(4'b1000), .E3(4'b0101),
    .out_10(eshkere_6_out_10));
  Eshkere eshkere_7 (
    .N(N6), .C0(C0), .C1(C1), .C2(C2), .C3(C3), .E0(4'b0110), .E1(4'b1001), .E2(4'b1100), .E3(4'b1111),
    .out_10(eshkere_7_out_10));
  Eshkere eshkere_8 (
    .N(N7), .C0(C0), .C1(C1), .C2(C2), .C3(C3), .E0(4'b1000), .E1(4'b0101), .E2(4'b0011), .E3(4'b1010),
    .out_10(eshkere_8_out_10));
  Eshkere eshkere_9 (
    .N(N8), .C0(C0), .C1(C1), .C2(C2), .C3(C3), .E0(4'b0000), .E1(4'b0110), .E2(4'b0111), .E3(4'b1011),
    .out_10(eshkere_9_out_10));
  Eshkere eshkere_10 (
    .N(N9), .C0(C0), .C1(C1), .C2(C2), .C3(C3), .E0(4'b1101), .E1(4'b0001), .E2(4'b0000), .E3(4'b1110),
    .out_10(eshkere_10_out_10));
  Eshkere eshkere_11 (
    .N(N10), .C0(C0), .C1(C1), .C2(C2), .C3(C3), .E0(4'b0011), .E1(4'b1101), .E2(4'b0100), .E3(4'b0001),
    .out_10(eshkere_11_out_10));
  Eshkere eshkere_12 (
    .N(N11), .C0(C0), .C1(C1), .C2(C2), .C3(C3), .E0(4'b0100), .E1(4'b1110), .E2(4'b1010), .E3(4'b0111),
    .out_10(eshkere_12_out_10));
  Eshkere eshkere_13 (
    .N(N12), .C0(C0), .C1(C1), .C2(C2), .C3(C3), .E0(4'b1110), .E1(4'b0000), .E2(4'b0001), .E3(4'b0110),
    .out_10(eshkere_13_out_10));
  Eshkere eshkere_14 (
    .N(N13), .C0(C0), .C1(C1), .C2(C2), .C3(C3), .E0(4'b0111), .E1(4'b1011), .E2(4'b1101), .E3(4'b0000),
    .out_10(eshkere_14_out_10));
  Eshkere eshkere_15 (
    .N(N14), .C0(C0), .C1(C1), .C2(C2), .C3(C3), .E0(4'b0101), .E1(4'b0011), .E2(4'b1011), .E3(4'b1000),
    .out_10(eshkere_15_out_10));
  Eshkere eshkere_16 (
    .N(N15), .C0(C0), .C1(C1), .C2(C2), .C3(C3), .E0(4'b1011), .E1(4'b1000), .E2(4'b0110), .E3(4'b1101),
    .out_10(eshkere_16_out_10));
  assign B8 = eshkere_1_out_10 | eshkere_10_out_10 | eshkere_2_out_10 | eshkere_11_out_10 | eshkere_3_out_10 | eshkere_12_out_10 | eshkere_4_out_10 | eshkere_13_out_10 | eshkere_5_out_10 | eshkere_14_out_10 | eshkere_6_out_10 | eshkere_15_out_10 | eshkere_7_out_10 | eshkere_16_out_10 | eshkere_8_out_10 | eshkere_9_out_10;  // OR_Gate or_1, 4 bits wide

  // Other names for the same wires on the sheet: B2 = in_1[0]; M4 = in_1[1]; M3 = in_1[2]; M2 = in_1[3]; M1 = in_1[4];
  //   B1 = in_1[5]
endmodule

module S7 (
  input  [5:0] in_1,
  output [3:0] B8
);

  wire C0, C1, C2, C3, N0, N1, N2, N3, N4, N5, N6, N7, N8, N9, N10, N11, N12, N13, N14, N15, not_1_out,
       not_2_out, not_3_out, not_4_out;
  wire [3:0] eshkere_1_out_10, eshkere_2_out_10, eshkere_3_out_10, eshkere_4_out_10, eshkere_5_out_10,
       eshkere_6_out_10, eshkere_7_out_10, eshkere_8_out_10, eshkere_9_out_10, eshkere_10_out_10,
       eshkere_11_out_10, eshkere_12_out_10, eshkere_13_out_10, eshkere_14_out_10, eshkere_15_out_10,
       eshkere_16_out_10;

  not not_1 (not_1_out, in_1[5]);
  and and_1 (C0, not_1_out, not_2_out);
  not not_2 (not_2_out, in_1[0]);
  and and_2 (C2, in_1[5], not_3_out);
  not not_3 (not_3_out, in_1[0]);
  not not_4 (not_4_out, in_1[5]);
  and and_3 (C1, not_4_out, in_1[0]);
  and and_4 (C3, in_1[5], in_1[0]);
  and and_5 (N0, ~in_1[4], ~in_1[3], ~in_1[2], ~in_1[1]);  // AND_Gate
  and and_6 (N1, ~in_1[4], ~in_1[3], ~in_1[2], in_1[1]);  // AND_Gate
  and and_7 (N2, ~in_1[4], ~in_1[3], in_1[2], ~in_1[1]);  // AND_Gate
  and and_8 (N3, ~in_1[4], ~in_1[3], in_1[2], in_1[1]);  // AND_Gate
  and and_9 (N4, ~in_1[4], in_1[3], ~in_1[2], ~in_1[1]);  // AND_Gate
  and and_10 (N5, ~in_1[4], in_1[3], ~in_1[2], in_1[1]);  // AND_Gate
  and and_11 (N6, ~in_1[4], in_1[3], in_1[2], ~in_1[1]);  // AND_Gate
  and and_12 (N7, ~in_1[4], in_1[3], in_1[2], in_1[1]);  // AND_Gate
  and and_13 (N8, in_1[4], ~in_1[3], ~in_1[2], ~in_1[1]);  // AND_Gate
  and and_14 (N9, in_1[4], ~in_1[3], ~in_1[2], in_1[1]);  // AND_Gate
  and and_15 (N10, in_1[4], ~in_1[3], in_1[2], ~in_1[1]);  // AND_Gate
  and and_16 (N11, in_1[4], ~in_1[3], in_1[2], in_1[1]);  // AND_Gate
  and and_17 (N12, in_1[4], in_1[3], ~in_1[2], ~in_1[1]);  // AND_Gate
  and and_18 (N13, in_1[4], in_1[3], ~in_1[2], in_1[1]);  // AND_Gate
  and and_19 (N14, in_1[4], in_1[3], in_1[2], ~in_1[1]);  // AND_Gate
  and and_20 (N15, in_1[4], in_1[3], in_1[2], in_1[1]);
  Eshkere eshkere_1 (
    .N(N0), .C0(C0), .C1(C1), .C2(C2), .C3(C3), .E0(4'b0100), .E1(4'b1101), .E2(4'b0001), .E3(4'b0110),
    .out_10(eshkere_1_out_10));
  Eshkere eshkere_2 (
    .N(N1), .C0(C0), .C1(C1), .C2(C2), .C3(C3), .E0(4'b1011), .E1(4'b0000), .E2(4'b0100), .E3(4'b1011),
    .out_10(eshkere_2_out_10));
  Eshkere eshkere_3 (
    .N(N2), .C0(C0), .C1(C1), .C2(C2), .C3(C3), .E0(4'b0010), .E1(4'b1011), .E2(4'b1011), .E3(4'b1101),
    .out_10(eshkere_3_out_10));
  Eshkere eshkere_4 (
    .N(N3), .C0(C0), .C1(C1), .C2(C2), .C3(C3), .E0(4'b1110), .E1(4'b0111), .E2(4'b1101), .E3(4'b1000),
    .out_10(eshkere_4_out_10));
  Eshkere eshkere_5 (
    .N(N4), .C0(C0), .C1(C1), .C2(C2), .C3(C3), .E0(4'b1111), .E1(4'b0100), .E2(4'b1100), .E3(4'b0001),
    .out_10(eshkere_5_out_10));
  Eshkere eshkere_6 (
    .N(N5), .C0(C0), .C1(C1), .C2(C2), .C3(C3), .E0(4'b0000), .E1(4'b1001), .E2(4'b0011), .E3(4'b0100),
    .out_10(eshkere_6_out_10));
  Eshkere eshkere_7 (
    .N(N6), .C0(C0), .C1(C1), .C2(C2), .C3(C3), .E0(4'b1000), .E1(4'b0001), .E2(4'b0111), .E3(4'b1010),
    .out_10(eshkere_7_out_10));
  Eshkere eshkere_8 (
    .N(N7), .C0(C0), .C1(C1), .C2(C2), .C3(C3), .E0(4'b1101), .E1(4'b1010), .E2(4'b1110), .E3(4'b0111),
    .out_10(eshkere_8_out_10));
  Eshkere eshkere_9 (
    .N(N8), .C0(C0), .C1(C1), .C2(C2), .C3(C3), .E0(4'b0011), .E1(4'b1110), .E2(4'b1010), .E3(4'b1001),
    .out_10(eshkere_9_out_10));
  Eshkere eshkere_10 (
    .N(N9), .C0(C0), .C1(C1), .C2(C2), .C3(C3), .E0(4'b1100), .E1(4'b0011), .E2(4'b1111), .E3(4'b0101),
    .out_10(eshkere_10_out_10));
  Eshkere eshkere_11 (
    .N(N10), .C0(C0), .C1(C1), .C2(C2), .C3(C3), .E0(4'b1001), .E1(4'b0101), .E2(4'b0110), .E3(4'b0000),
    .out_10(eshkere_11_out_10));
  Eshkere eshkere_12 (
    .N(N11), .C0(C0), .C1(C1), .C2(C2), .C3(C3), .E0(4'b0111), .E1(4'b1100), .E2(4'b1000), .E3(4'b1111),
    .out_10(eshkere_12_out_10));
  Eshkere eshkere_13 (
    .N(N12), .C0(C0), .C1(C1), .C2(C2), .C3(C3), .E0(4'b0101), .E1(4'b0010), .E2(4'b0000), .E3(4'b1110),
    .out_10(eshkere_13_out_10));
  Eshkere eshkere_14 (
    .N(N13), .C0(C0), .C1(C1), .C2(C2), .C3(C3), .E0(4'b1010), .E1(4'b1111), .E2(4'b0101), .E3(4'b0010),
    .out_10(eshkere_14_out_10));
  Eshkere eshkere_15 (
    .N(N14), .C0(C0), .C1(C1), .C2(C2), .C3(C3), .E0(4'b0110), .E1(4'b1000), .E2(4'b1001), .E3(4'b0011),
    .out_10(eshkere_15_out_10));
  Eshkere eshkere_16 (
    .N(N15), .C0(C0), .C1(C1), .C2(C2), .C3(C3), .E0(4'b0001), .E1(4'b0110), .E2(4'b0010), .E3(4'b1100),
    .out_10(eshkere_16_out_10));
  assign B8 = eshkere_1_out_10 | eshkere_10_out_10 | eshkere_2_out_10 | eshkere_11_out_10 | eshkere_3_out_10 | eshkere_12_out_10 | eshkere_4_out_10 | eshkere_13_out_10 | eshkere_5_out_10 | eshkere_14_out_10 | eshkere_6_out_10 | eshkere_15_out_10 | eshkere_7_out_10 | eshkere_16_out_10 | eshkere_8_out_10 | eshkere_9_out_10;  // OR_Gate or_1, 4 bits wide

  // Other names for the same wires on the sheet: B2 = in_1[0]; M4 = in_1[1]; M3 = in_1[2]; M2 = in_1[3]; M1 = in_1[4];
  //   B1 = in_1[5]
endmodule

module S8 (
  input  [5:0] in_1,
  output [3:0] B8
);

  wire C0, C1, C2, C3, N0, N1, N2, N3, N4, N5, N6, N7, N8, N9, N10, N11, N12, N13, N14, N15;
  wire [3:0] eshkere_1_out_10, eshkere_2_out_10, eshkere_3_out_10, eshkere_4_out_10, eshkere_5_out_10,
       eshkere_6_out_10, eshkere_7_out_10, eshkere_8_out_10, eshkere_9_out_10, eshkere_10_out_10,
       eshkere_11_out_10, eshkere_12_out_10, eshkere_13_out_10, eshkere_14_out_10, eshkere_15_out_10,
       eshkere_16_out_10;

  and and_1 (C0, ~in_1[5], ~in_1[0]);  // AND_Gate
  and and_2 (C2, in_1[5], ~in_1[0]);  // AND_Gate
  and and_3 (C1, ~in_1[5], in_1[0]);  // AND_Gate
  and and_4 (C3, in_1[5], in_1[0]);
  and and_5 (N0, ~in_1[4], ~in_1[3], ~in_1[2], ~in_1[1]);  // AND_Gate
  and and_6 (N1, ~in_1[4], ~in_1[3], ~in_1[2], in_1[1]);  // AND_Gate
  and and_7 (N2, ~in_1[4], ~in_1[3], in_1[2], ~in_1[1]);  // AND_Gate
  and and_8 (N3, ~in_1[4], ~in_1[3], in_1[2], in_1[1]);  // AND_Gate
  and and_9 (N4, ~in_1[4], in_1[3], ~in_1[2], ~in_1[1]);  // AND_Gate
  and and_10 (N5, ~in_1[4], in_1[3], ~in_1[2], in_1[1]);  // AND_Gate
  and and_11 (N6, ~in_1[4], in_1[3], in_1[2], ~in_1[1]);  // AND_Gate
  and and_12 (N7, ~in_1[4], in_1[3], in_1[2], in_1[1]);  // AND_Gate
  and and_13 (N8, in_1[4], ~in_1[3], ~in_1[2], ~in_1[1]);  // AND_Gate
  and and_14 (N9, in_1[4], ~in_1[3], ~in_1[2], in_1[1]);  // AND_Gate
  and and_15 (N10, in_1[4], ~in_1[3], in_1[2], ~in_1[1]);  // AND_Gate
  and and_16 (N11, in_1[4], ~in_1[3], in_1[2], in_1[1]);  // AND_Gate
  and and_17 (N12, in_1[4], in_1[3], ~in_1[2], ~in_1[1]);  // AND_Gate
  and and_18 (N13, in_1[4], in_1[3], ~in_1[2], in_1[1]);  // AND_Gate
  and and_19 (N14, in_1[4], in_1[3], in_1[2], ~in_1[1]);  // AND_Gate
  and and_20 (N15, in_1[4], in_1[3], in_1[2], in_1[1]);
  Eshkere eshkere_1 (
    .N(N0), .C0(C0), .C1(C1), .C2(C2), .C3(C3), .E0(4'b1101), .E1(4'b0001), .E2(4'b0111), .E3(4'b0010),
    .out_10(eshkere_1_out_10));
  Eshkere eshkere_2 (
    .N(N1), .C0(C0), .C1(C1), .C2(C2), .C3(C3), .E0(4'b0010), .E1(4'b1111), .E2(4'b1011), .E3(4'b0001),
    .out_10(eshkere_2_out_10));
  Eshkere eshkere_3 (
    .N(N2), .C0(C0), .C1(C1), .C2(C2), .C3(C3), .E0(4'b1000), .E1(4'b1101), .E2(4'b0100), .E3(4'b1110),
    .out_10(eshkere_3_out_10));
  Eshkere eshkere_4 (
    .N(N3), .C0(C0), .C1(C1), .C2(C2), .C3(C3), .E0(4'b0100), .E1(4'b1000), .E2(4'b0001), .E3(4'b0111),
    .out_10(eshkere_4_out_10));
  Eshkere eshkere_5 (
    .N(N4), .C0(C0), .C1(C1), .C2(C2), .C3(C3), .E0(4'b0110), .E1(4'b1010), .E2(4'b1001), .E3(4'b0100),
    .out_10(eshkere_5_out_10));
  Eshkere eshkere_6 (
    .N(N5), .C0(C0), .C1(C1), .C2(C2), .C3(C3), .E0(4'b1111), .E1(4'b0011), .E2(4'b1100), .E3(4'b1010),
    .out_10(eshkere_6_out_10));
  Eshkere eshkere_7 (
    .N(N6), .C0(C0), .C1(C1), .C2(C2), .C3(C3), .E0(4'b1011), .E1(4'b0111), .E2(4'b1110), .E3(4'b1000),
    .out_10(eshkere_7_out_10));
  Eshkere eshkere_8 (
    .N(N7), .C0(C0), .C1(C1), .C2(C2), .C3(C3), .E0(4'b0001), .E1(4'b0100), .E2(4'b0010), .E3(4'b1101),
    .out_10(eshkere_8_out_10));
  Eshkere eshkere_9 (
    .N(N8), .C0(C0), .C1(C1), .C2(C2), .C3(C3), .E0(4'b1010), .E1(4'b1100), .E2(4'b0000), .E3(4'b1111),
    .out_10(eshkere_9_out_10));
  Eshkere eshkere_10 (
    .N(N9), .C0(C0), .C1(C1), .C2(C2), .C3(C3), .E0(4'b1001), .E1(4'b0101), .E2(4'b0110), .E3(4'b1100),
    .out_10(eshkere_10_out_10));
  Eshkere eshkere_11 (
    .N(N10), .C0(C0), .C1(C1), .C2(C2), .C3(C3), .E0(4'b0011), .E1(4'b0110), .E2(4'b1010), .E3(4'b1001),
    .out_10(eshkere_11_out_10));
  Eshkere eshkere_12 (
    .N(N11), .C0(C0), .C1(C1), .C2(C2), .C3(C3), .E0(4'b1110), .E1(4'b1011), .E2(4'b1101), .E3(4'b0000),
    .out_10(eshkere_12_out_10));
  Eshkere eshkere_13 (
    .N(N12), .C0(C0), .C1(C1), .C2(C2), .C3(C3), .E0(4'b0101), .E1(4'b0000), .E2(4'b1111), .E3(4'b0011),
    .out_10(eshkere_13_out_10));
  Eshkere eshkere_14 (
    .N(N13), .C0(C0), .C1(C1), .C2(C2), .C3(C3), .E0(4'b0000), .E1(4'b1110), .E2(4'b0011), .E3(4'b0101),
    .out_10(eshkere_14_out_10));
  Eshkere eshkere_15 (
    .N(N14), .C0(C0), .C1(C1), .C2(C2), .C3(C3), .E0(4'b1100), .E1(4'b1001), .E2(4'b0101), .E3(4'b0110),
    .out_10(eshkere_15_out_10));
  Eshkere eshkere_16 (
    .N(N15), .C0(C0), .C1(C1), .C2(C2), .C3(C3), .E0(4'b0111), .E1(4'b0010), .E2(4'b1000), .E3(4'b1011),
    .out_10(eshkere_16_out_10));
  assign B8 = eshkere_1_out_10 | eshkere_10_out_10 | eshkere_2_out_10 | eshkere_11_out_10 | eshkere_3_out_10 | eshkere_12_out_10 | eshkere_4_out_10 | eshkere_13_out_10 | eshkere_5_out_10 | eshkere_14_out_10 | eshkere_6_out_10 | eshkere_15_out_10 | eshkere_7_out_10 | eshkere_16_out_10 | eshkere_8_out_10 | eshkere_9_out_10;  // OR_Gate or_1, 4 bits wide

  // Other names for the same wires on the sheet: B2 = in_1[0]; M4 = in_1[1]; M3 = in_1[2]; M2 = in_1[3]; M1 = in_1[4];
  //   B1 = in_1[5]
endmodule

module separation (
  input  [5:0] in_1,
  output [1:0] border,
  output [3:0] middle
);


  assign border = {in_1[5], in_1[0]};
  assign middle = in_1[4:1];
endmodule

module joining (
  input  [27:0] C,
  input  [27:0] D,
  output [47:0] Key
);


  assign Key = {C[14], C[11], C[17], C[4], C[27], C[23], C[25], C[0], C[13], C[22], C[7], C[18], C[5], C[9], C[16], C[24], C[2], C[20], C[12], C[21], C[1], C[8], C[15], C[26], D[15], D[4], D[25], D[19], D[9], D[1], D[26], D[16], D[5], D[11], D[23], D[8], D[12], D[7], D[17], D[0], D[22], D[3], D[10], D[14], D[6], D[20], D[27], D[24]};

  // Other names for the same wires on the sheet: i25 = C[3]; i22 = C[6]; i18 = C[10]; i9 = C[19]; i54 = D[2];
  //   i43 = D[13]; i38 = D[18]; i35 = D[21]; i32 = D[24]; i29 = D[27]; i36 = D[20]; i50 = D[6]; i42 = D[14];
  //   i46 = D[10]; i53 = D[3]; i34 = D[22]; i56 = D[0]; i39 = D[17]; i49 = D[7]; i44 = D[12]; i48 = D[8]; i33 = D[23];
  //   i45 = D[11]; i51 = D[5]; i40 = D[16]; i30 = D[26]; i55 = D[1]; i47 = D[9]; i37 = D[19]; i31 = D[25]; i52 = D[4];
  //   i41 = D[15]; i2 = C[26]; i13 = C[15]; i20 = C[8]; i27 = C[1]; i7 = C[21]; i16 = C[12]; i8 = C[20]; i26 = C[2];
  //   i4 = C[24]; i12 = C[16]; i19 = C[9]; i23 = C[5]; i10 = C[18]; i21 = C[7]; i6 = C[22]; i15 = C[13]; i28 = C[0];
  //   i3 = C[25]; i5 = C[23]; i1 = C[27]; i24 = C[4]; i11 = C[17]; i17 = C[11]; i14 = C[14]
endmodule

module Eshkere (
  input  N,
  input  C0,
  input  C1,
  input  C2,
  input  C3,
  input  [3:0] E0,
  input  [3:0] E1,
  input  [3:0] E2,
  input  [3:0] E3,
  output [3:0] out_10
);

  wire [3:0] and_5_out, and_6_out, and_7_out, and_8_out;
  wire [3:3] and_1_out, and_2_out, and_3_out, and_4_out;

  and and_1 (and_1_out[3], N, C0);
  and and_2 (and_2_out[3], N, C1);
  and and_3 (and_3_out[3], N, C2);
  and and_4 (and_4_out[3], N, C3);
  assign and_5_out = E0 & {4{and_1_out[3]}};  // AND_Gate and_5, 4 bits wide
  assign and_6_out = E1 & {4{and_2_out[3]}};  // AND_Gate and_6, 4 bits wide
  assign and_7_out = E2 & {4{and_3_out[3]}};  // AND_Gate and_7, 4 bits wide
  assign and_8_out = E3 & {4{and_4_out[3]}};  // AND_Gate and_8, 4 bits wide
  assign out_10 = and_5_out | and_6_out | and_7_out | and_8_out;  // OR_Gate or_1, 4 bits wide
endmodule

module MUX (
  input  [47:0] in_1,
  output [31:0] out_2,
  output [31:0] o1
);

  // Probe on in_1[47:42]
  S8 s8_1 (.in_1(in_1[5:0]), .B8({o1[27], o1[5], o1[17], o1[11]}));
  S7 s7_1 (.in_1(in_1[11:6]), .B8({o1[0], o1[20], o1[10], o1[25]}));
  S6 s6_1 (.in_1(in_1[17:12]), .B8({o1[28], o1[3], o1[21], o1[13]}));
  S5 s5_1 (.in_1(in_1[23:18]), .B8({o1[24], o1[18], o1[7], o1[29]}));
  S4 s4_1 (.in_1(in_1[29:24]), .B8({o1[6], o1[12], o1[22], o1[31]}));
  S3 s3_1 (.in_1(in_1[35:30]), .B8({o1[8], o1[16], o1[2], o1[26]}));
  S2 s2_1 (.in_1(in_1[41:36]), .B8({o1[19], o1[4], o1[30], o1[14]}));
  S1 s1_1 (.in_1(in_1[47:42]), .B8({o1[23], o1[15], o1[9], o1[1]}));
  // Probe on {o1[23], o1[15], o1[9], o1[1]}

  assign out_2 = {o1[23], o1[15], o1[9], o1[1], o1[19], o1[4], o1[30], o1[14], o1[8], o1[16], o1[2], o1[26], o1[6], o1[12], o1[22], o1[31], o1[24], o1[18], o1[7], o1[29:28], o1[3], o1[21], o1[13], o1[0], o1[20], o1[10], o1[25], o1[27], o1[5], o1[17], o1[11]};

  // Other names for the same wires on the sheet: i25 = o1[0]; i4 = o1[1]; i11 = o1[2]; i22 = o1[3]; i6 = o1[4];
  //   i30 = o1[5]; i13 = o1[6]; i19 = o1[7]; i9 = o1[8]; i3 = o1[9]; i27 = o1[10]; i32 = o1[11]; i14 = o1[12];
  //   i24 = o1[13]; i8 = o1[14]; i2 = o1[15]; i10 = o1[16]; i31 = o1[17]; i18 = o1[18]; i5 = o1[19]; i26 = o1[20];
  //   i23 = o1[21]; i15 = o1[22]; i1 = o1[23]; i17 = o1[24]; i28 = o1[25]; i12 = o1[26]; i29 = o1[27]; i21 = o1[28];
  //   i20 = o1[29]; i7 = o1[30]; i16 = o1[31]
endmodule

module circle (
  input  [47:0] key,
  input  [31:0] Ri,
  input  [31:0] Li,
  output [31:0] R_i,
  output [31:0] L_i
);

  wire [31:0] mux_1_o1;
  wire [47:0] expansion_e_1_out_2, xor_1_out;

  Expansion_E expansion_e_1 (.in_1(Ri), .out_2(expansion_e_1_out_2));
  assign xor_1_out = key ^ expansion_e_1_out_2;  // XOR_Gate xor_1, 48 bits wide
  MUX mux_1 (.in_1(xor_1_out), .o1(mux_1_o1));  // open: out_2
  assign R_i = mux_1_o1 ^ Li;  // XOR_Gate xor_2, 32 bits wide

  assign L_i = Ri;
endmodule

module FinalPermutation (
  input  [31:0] L,
  input  [31:0] R,
  output [63:0] IP_ans
);


  assign IP_ans = {L[24], R[24], L[16], R[16], L[8], R[8], L[0], R[0], L[25], R[25], L[17], R[17], L[9], R[9], L[1], R[1], L[26], R[26], L[18], R[18], L[10], R[10], L[2], R[2], L[27], R[27], L[19], R[19], L[11], R[11], L[3], R[3], L[28], R[28], L[20], R[20], L[12], R[12], L[4], R[4], L[29], R[29], L[21], R[21], L[13], R[13], L[5], R[5], L[30], R[30], L[22], R[22], L[14], R[14], L[6], R[6], L[31], R[31], L[23], R[23], L[15], R[15], L[7], R[7]};

  // Other names for the same wires on the sheet: i25 = R[7]; i57 = L[7]; i17 = R[15]; i49 = L[15]; i9 = R[23];
  //   i41 = L[23]; i1 = R[31]; i33 = L[31]; i26 = R[6]; i58 = L[6]; i18 = R[14]; i50 = L[14]; i10 = R[22];
  //   i42 = L[22]; i2 = R[30]; i34 = L[30]; i27 = R[5]; i59 = L[5]; i19 = R[13]; i51 = L[13]; i11 = R[21];
  //   i43 = L[21]; i3 = R[29]; i35 = L[29]; i28 = R[4]; i60 = L[4]; i20 = R[12]; i52 = L[12]; i12 = R[20];
  //   i44 = L[20]; i4 = R[28]; i36 = L[28]; i29 = R[3]; i61 = L[3]; i21 = R[11]; i53 = L[11]; i13 = R[19];
  //   i45 = L[19]; i5 = R[27]; i37 = L[27]; i30 = R[2]; i62 = L[2]; i22 = R[10]; i54 = L[10]; i14 = R[18];
  //   i46 = L[18]; i6 = R[26]; i38 = L[26]; i31 = R[1]; i63 = L[1]; i23 = R[9]; i55 = L[9]; i15 = R[17]; i47 = L[17];
  //   i7 = R[25]; i39 = L[25]; i32 = R[0]; i64 = L[0]; i24 = R[8]; i56 = L[8]; i16 = R[16]; i48 = L[16]; i8 = R[24];
  //   i40 = L[24]
endmodule

module reversecircle (
  input  [47:0] key,
  input  [31:0] Li,
  input  [31:0] Ri,
  output [31:0] L_i,
  output [31:0] R_i
);

  wire [31:0] mux_1_o1;
  wire [47:0] expansion_e_1_out_2, xor_1_out;

  Expansion_E expansion_e_1 (.in_1(Li), .out_2(expansion_e_1_out_2));
  assign xor_1_out = key ^ expansion_e_1_out_2;  // XOR_Gate xor_1, 48 bits wide
  MUX mux_1 (.in_1(xor_1_out), .o1(mux_1_o1));  // open: out_2
  assign L_i = mux_1_o1 ^ Ri;  // XOR_Gate xor_2, 32 bits wide

  assign R_i = Li;
endmodule
